# Fritzing sketch Controller (saved by Fritzing 0.9.3b)

parts:
  Part2 = Photon  # not connected
  Part1 = Particle Relay Shield
  L2 = Solenoid
  J1 = Camdenboss CTB0158-7 [part_number=CTB0158-7 package=THT]
  J2 = Camdenboss CTB0158-7 [part_number=CTB0158-7 package=THT]
  L3 = Solenoid
  J3 = Power Jack [package=power_jack_slot]

nets:
  N1: Part1.NC1, J1.terminal_7
  N2: Part1.MAIN1, Part1.MAIN2, J3.GNDBREAK
  N3: Part1.NC2, J1.terminal_5
  N4: L2.pin1, J2.terminal_4
  N5: L2.pin2, J2.terminal_3
  N6: J1.terminal_4, J1.terminal_6, J3.GND
  N7: J2.terminal_1, L3.pin2
  N8: J2.terminal_2, L3.pin1
